# Fritzing sketch mvs-usb-2btn (saved by Fritzing 0.9.5d)
breadboards: 1

parts:
  IC1 = ULN2803A [package=THT]
  R1 = Resistor [tolerance=±5% resistance=2.2k package=THT]
  R2 = Resistor [tolerance=±5% resistance=2.2k package=THT]
  R3 = Resistor [tolerance=±5% resistance=2.2k package=THT]
  R4 = Resistor [tolerance=±5% resistance=2.2k package=THT]
  R5 = Resistor [tolerance=±5% resistance=2.2k package=THT]
  R6 = Resistor [tolerance=±5% resistance=2.2k package=THT]
  R7 = Resistor [tolerance=±5% resistance=2.2k package=THT]
  R1-R8 = Resistor [tolerance=±5% resistance=2.2k package=THT]
  Mod1 = Raspberry Pi Pico

nets:
  N1: IC1.In_1, R1.Pin_0, R1.Pin_1, Mod1.pin_4
  N2: IC1.In_2, R2.Pin_0, R2.Pin_1, Mod1.pin_5
  N3: IC1.In_3, R5.Pin_0, R5.Pin_1, Mod1.pin_6
  N4: IC1.In_4, R7.Pin_0, R7.Pin_1, Mod1.pin_7
  N5: IC1.In_5, R4.Pin_0, R4.Pin_1, Mod1.pin_3, Mod1.pin_8, Mod1.pin_13, Mod1.pin_18, Mod1.pin_23, Mod1.pin_28, Mod1.pin_33, Mod1.pin_38, Mod1.pin_42
  N6: IC1.In_6, R3.Pin_0, R3.Pin_1, Mod1.pin_9
  N7: IC1.In_7, R6.Pin_0, R6.Pin_1, Mod1.pin_10
  N8: IC1.In_8, R1-R8.Pin_0, R1-R8.Pin_1, Mod1.pin_11

notes:
  to MVS JAMMA
  blue: up
  red: down
  yellow: right
  green: left
  white: A
  orange: B
  purple: coin
  pink: start
  MVS pin 27 (ground)
  MVS pin 3 or 4 -> +5v
  MVS pin 1,2,27 or 28 -> GND

custom parts:
  Raspberry Pi Pico: Raspberry Pi Pico. Based around the RP2040 microcontroller the Pico is a low cost microcontroller device bringing Raspberry Pi quality, cost, and easy of use to the microcontroller space. Jan 2021, Split part in to two versions: tht (this one) and SMD. This one will drill holes for a .1 in header in pcb to allow plugging in the module as well as providing pads to solder the module to the top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
