# Fritzing sketch mvs-usb-4btn (saved by Fritzing 0.9.5d)
breadboards: 2

parts:
  R1 = Resistor [tolerance=±5% resistance=2.2k package=THT]
  R2 = Resistor [tolerance=±5% resistance=2.2k package=THT]
  R3 = Resistor [tolerance=±5% resistance=2.2k package=THT]
  R4 = Resistor [tolerance=±5% resistance=2.2k package=THT]
  R5 = Resistor [tolerance=±5% resistance=2.2k package=THT]
  R6 = Resistor [tolerance=±5% resistance=2.2k package=THT]
  R7 = Resistor [tolerance=±5% resistance=2.2k package=THT]
  R1-R10 = Resistor [tolerance=±5% resistance=2.2k package=THT]
  Mod1 = Raspberry Pi Pico
  R11 = Resistor [tolerance=±5% resistance=2.2k package=THT]
  R12 = Resistor [tolerance=±5% resistance=2.2k package=THT]
  IC3 = ULN2003A [package="DIP16 [THT]"]
  IC1 = ULN2803A [package=THT]

nets:
  N1: R1.Pin_0, R1.Pin_1, Mod1.pin_4, IC1.In_1
  N2: R2.Pin_0, R2.Pin_1, Mod1.pin_5, IC1.In_2
  N3: R3.Pin_0, R3.Pin_1, Mod1.pin_9, IC1.In_6
  N4: R4.Pin_0, R4.Pin_1, Mod1.pin_3, Mod1.pin_8, Mod1.pin_13, Mod1.pin_18, Mod1.pin_23, Mod1.pin_28, Mod1.pin_33, Mod1.pin_38, Mod1.pin_42, R11.Pin_0, R11.Pin_1, IC3.In_2, IC1.In_5
  N5: R5.Pin_0, R5.Pin_1, Mod1.pin_6, IC1.In_3
  N6: R6.Pin_0, R6.Pin_1, Mod1.pin_10, IC1.In_7
  N7: R7.Pin_0, R7.Pin_1, Mod1.pin_7, IC1.In_4
  N8: R1-R10.Pin_0, R1-R10.Pin_1, Mod1.pin_11, IC1.In_8
  N9: Mod1.pin_12, R12.Pin_0, R12.Pin_1, IC3.In_1

notes:
  to MVS JAMMA
  blue: up -> 18
  red: down -> 19
  yellow: right -> 21
  green: left -> 20
  white: A -> 22
  orange: B -> 23
  ochra: C -> 22
  brow: D -> 23
  purple: coin -> 16
  pink: start -> 17
  MVS pin 27 (ground)
  MVS pin 27 or 28 (ground)
  MVS pin 3 or 4 -> +5v
  MVS pin 1,2,27 or 28 -> GND

custom parts:
  Raspberry Pi Pico: Raspberry Pi Pico. Based around the RP2040 microcontroller the Pico is a low cost microcontroller device bringing Raspberry Pi quality, cost, and easy of use to the microcontroller space. Jan 2021, Split part in to two versions: tht (this one) and SMD. This one will drill holes for a .1 in header in pcb to allow plugging in the module as well as providing pads to solder the module to the top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
